# Fritzing sketch pong (saved by Fritzing 0.9.3b)
breadboards: 1

parts:
  Bauteil1 = Arduino Nano (Rev3.0)
  Start_Switch = Pushbutton [package="[SMD]"]
  Piezo_Speaker = Piezo Speaker
  Paddle_2 = Rotary Potentiometer (Large) [maximum_resistance=10kΩ package=THT]
  Paddle_1 = Rotary Potentiometer (Large) [maximum_resistance=10kΩ package=THT]
  R1 = Resistor [tolerance=±5% resistance=10k package="0805 [SMD]"]
  Analog_TV_Out = RCA [package=rca]
  R2 = Resistor [tolerance=±5% resistance=470 package="0402 [SMD]"]
  R3 = Resistor [tolerance=±5% resistance=1k package="0402 [SMD]"]
  Paddle_3 = Rotary Potentiometer (Large) [maximum_resistance=10kΩ package=THT]
  Paddle_4 = Rotary Potentiometer (Large) [maximum_resistance=10kΩ package=THT]

nets:
  N1: Bauteil1.GND, Piezo_Speaker.pin1, Paddle_2.leg2, Paddle_1.leg2, R1.Pin_1, Analog_TV_Out.SHELL, Paddle_3.leg2, Paddle_4.leg2
  N2: Bauteil1.D2, Start_Switch.Pin_1, Start_Switch.Pin_2, R1.Pin_0
  N3: Bauteil1.D7, R3.Pin_0
  N4: Bauteil1.D9, R2.Pin_0
  N5: Bauteil1.D10, Piezo_Speaker.pin2
  N6: Bauteil1.5V, Start_Switch.Pin_3, Start_Switch.Pin_4, Paddle_2.leg1, Paddle_1.leg1, Paddle_3.leg1, Paddle_4.leg1
  N7: Bauteil1.A3, Paddle_4.wiper
  N8: Bauteil1.A2, Paddle_3.wiper
  N9: Bauteil1.A1, Paddle_1.wiper
  N10: Bauteil1.A0, Paddle_2.wiper
  N11: Analog_TV_Out.PIN, R2.Pin_1, R3.Pin_1
